# Fritzing sketch CHRISTMAS_IOT (saved by Fritzing 0.9.3b)
circuit board: 5.5cm x 4.5cm
breadboards: 1

parts:
  XTAL1 = Crystal [frequency="16 Mhz" package=THT]
  C1 = Ceramic Capacitor [capacitance=22pF package="100 mil [THT, multilayer]"]
  C2 = Ceramic Capacitor [capacitance=22pF package="100 mil [THT, multilayer]"]
  R1 = Resistor [tolerance=±5% resistance=10k package=THT]
  RESET1 = Pushbutton [package="[THT]"]
  C3 = Ceramic Capacitor [capacitance=100nF package="100 mil [THT, multilayer]"]
  R2 = Resistor [tolerance=±5% resistance=10k package=THT]
  RESET2 = Pushbutton [package="[THT]"]
  LEDSTRIP = female pin header, 3 pins [form="♀ (female)"]
  LS5V = female pin header, 4 pins [form="♀ (female)"]
  LS3_3V = female pin header, 4 pins [form="♀ (female)"]
  C4 = Electrolytic Capacitor [capacitance=0.1mF voltage=16V package="200 mil [THT, electrolytic]"]
  VIN = screw terminal, 2 pins
  C5 = Electrolytic Capacitor [capacitance=10µF voltage=16V package="100 mil [THT, electrolytic]"]
  U3 = Voltage Regulator - 3.3V [package="TO220 [THT]"]
  U2 = atmega328 [package=dip]
  Espessif_Serial_Wifi_Modul_1 = ESP8266 ESP01 [part_number=ESP8266 package=THT]

nets:
  N1: XTAL1.pin_0, C2.1, U2.XLAT1
  N2: XTAL1.pin_1, C1.1, U2.XLAT2
  GND: C1.0, C2.0, RESET1.Pin_3, RESET1.Pin_4, C3.1, RESET2.Pin_3, RESET2.Pin_4, LEDSTRIP.pin3, LS5V.pin3, LS3_3V.pin3, C4.-, VIN.pin1, C5.-, U3.GND, U2.GND, Espessif_Serial_Wifi_Modul_1.GND
  5V: R1.Pin_0, C3.0, LEDSTRIP.pin1, LS5V.pin4, C4.+, VIN.pin2, U3.input_voltage, U2.VCC, U2.AVCC, U2.AREF
  N3: R1.Pin_1, RESET1.Pin_1, RESET1.Pin_2, U2.RESET
  N4: R2.Pin_0, RESET2.Pin_1, RESET2.Pin_2, Espessif_Serial_Wifi_Modul_1.GPIO16
  3.3V: R2.Pin_1, LS3_3V.pin4, C5.+, U3.output_voltage, Espessif_Serial_Wifi_Modul_1.VCC, Espessif_Serial_Wifi_Modul_1.CH_PD
  DATA: LEDSTRIP.pin2, U2.D9_(PWM)
  TX: LS5V.pin1, U2.D1_(TX)
  RX: LS5V.pin2, U2.D0_(RX)
  N5: LS3_3V.pin1, Espessif_Serial_Wifi_Modul_1.RXD
  N6: LS3_3V.pin2, Espessif_Serial_Wifi_Modul_1.TXD

notes:
  +
  -

custom parts:
  ESP8266 ESP01: Generic WiFi Module based on the ESP8266 with onboard PCB antenna and UART communications
