# Fritzing sketch SWITCH_IOT (saved by Fritzing 0.9.3b)
circuit board: 6cm x 4cm
breadboards: 1

parts:
  Espessif_Serial_Wifi_Modul_1 = ESP8266 ESP01 [part_number=ESP8266 package=THT]
  R1 = Resistor [tolerance=±5% resistance=10k package=THT]
  R2 = Resistor [tolerance=±5% resistance=10k package=THT]
  R3 = Resistor [tolerance=±5% resistance=1k package=THT]
  C1 = Electrolytic Capacitor [capacitance=1000μF package="200 mil [THT, electrolytic]"]
  VC- = female pin header, 1 pin [form="♀ (female)"]
  VC+ = female pin header, 1 pin [form="♀ (female)"]
  V1 = DC Power [voltage=5]
  V2 = AC Power [voltage=5 frequency=60]
  U1 = OMRON G3MB-202p [package=relay-s108t02]
  AC2 = female pin header, 1 pin [form="♀ (female)"]
  AC1 = female pin header, 1 pin [form="♀ (female)"]
  Q1 = TRANSISTOR_PNP [package=to-92]
  OUT = screw terminal, 3 pins
  IN = screw terminal, 3 pins
  F1 = Resettable Fuse PTC [package=ptc]

nets:
  GND: Espessif_Serial_Wifi_Modul_1.GND, C1.-, VC-.pin1, V1.V-, U1.-, OUT.pin1, IN.pin1
  N1: Espessif_Serial_Wifi_Modul_1.VCC, Espessif_Serial_Wifi_Modul_1.CH_PD, R1.Pin_1, R3.Pin_0, C1.+, VC+.pin1, V1.V+, Q1.E
  N2: Espessif_Serial_Wifi_Modul_1.GPIO16, R3.Pin_1
  N3: Espessif_Serial_Wifi_Modul_1.GPIO00, R2.Pin_0
  N4: R1.Pin_0, R2.Pin_1, Q1.B
  N5: V2.V+, AC1.pin1, IN.pin3, F1.1
  N6: V2.V-, AC2.pin1, OUT.pin2, IN.pin2
  N7: U1.T1, F1.2
  N8: U1.T2, OUT.pin3
  N9: U1.+, Q1.C

custom parts:
  ESP8266 ESP01: Generic WiFi Module based on the ESP8266 with onboard PCB antenna and UART communications
  OMRON G3MB-202p: SPST SS relay
